// Digital circuit 4bit alu.dig as structural Verilog
module _4bit_alu (
  input  [3:0] in_1
);

  wire _7404_1_pin2, _7404_1_pin4, _7404_1_pin6, _7404_1_pin8, _7404_1_pin10, _7404_1_pin12, _74173_1_pin3,
       _74173_1_pin4, _74173_1_pin5, _74173_1_pin6, _74173_2_pin3, _74173_2_pin4, _74173_2_pin5,
       _74173_2_pin6, _74283_1_pin1, _74283_1_pin4, _74283_1_pin9, _74283_1_pin10, _74283_1_pin13, CLK, LDA,
       LDB, WALU;
  wire [3:0] _74126_1_pin3;

  Button button_1 (.out(CLK));
  DipSwitch #(.dipDefault("true")) dipswitch_1 (.out(LDA));
  DipSwitch #(.dipDefault("true")) dipswitch_2 (.out(LDB));
  DipSwitch dipswitch_3 (.out(WALU));
  _74173 _74173_1 (
    .pin1(1'b0), .pin2(1'b0), .pin3(_74173_1_pin3), .pin4(_74173_1_pin4), .pin5(_74173_1_pin5),
    .pin6(_74173_1_pin6), .pin7(CLK), .pin8(1'b0), .pin9(LDB), .pin10(1'b0), .pin11(in_1[3]),
    .pin12(in_1[2]), .pin13(in_1[1]), .pin14(in_1[0]), .pin15(1'b0), .pin16(1'b1));
  _7404 _7404_1 (
    .pin1(_74173_1_pin3), .pin2(_7404_1_pin2), .pin3(_74173_1_pin4), .pin4(_7404_1_pin4), .pin5(1'b0),
    .pin6(_7404_1_pin6), .pin7(1'b0), .pin8(_7404_1_pin8), .pin9(1'b0), .pin10(_7404_1_pin10),
    .pin11(_74173_1_pin6), .pin12(_7404_1_pin12), .pin13(_74173_1_pin5), .pin14(1'b1));
  LED led_1 (.in(_7404_1_pin6));
  LED led_2 (.in(_7404_1_pin8));
  _74173 _74173_2 (
    .pin1(1'b0), .pin2(1'b0), .pin3(_74173_2_pin3), .pin4(_74173_2_pin4), .pin5(_74173_2_pin5),
    .pin6(_74173_2_pin6), .pin7(CLK), .pin8(1'b0), .pin9(LDA), .pin10(1'b0), .pin11(in_1[3]),
    .pin12(in_1[2]), .pin13(in_1[1]), .pin14(in_1[0]), .pin15(1'b0), .pin16(1'b1));
  _74283 _74283_1 (
    .pin1(_74283_1_pin1), .pin2(_7404_1_pin4), .pin3(_74173_2_pin4), .pin4(_74283_1_pin4),
    .pin5(_74173_2_pin3), .pin6(_7404_1_pin2), .pin7(1'b1), .pin8(1'b0), .pin9(_74283_1_pin9),
    .pin10(_74283_1_pin10), .pin11(_7404_1_pin10), .pin12(_74173_2_pin6), .pin13(_74283_1_pin13),
    .pin14(_74173_2_pin5), .pin15(_7404_1_pin12), .pin16(1'b1));
  LED led_3 (.in(_74283_1_pin9));
  _74126 _74126_1 (
    .pin1(WALU), .pin2(_74283_1_pin4), .pin3(_74126_1_pin3[0]), .pin4(WALU), .pin5(_74283_1_pin1),
    .pin6(_74126_1_pin3[1]), .pin7(1'b0), .pin8(_74126_1_pin3[2]), .pin9(_74283_1_pin13), .pin10(WALU),
    .pin11(_74126_1_pin3[3]), .pin12(_74283_1_pin10), .pin13(WALU), .pin14(1'b1));
  Seven_Seg_Hex seven_seg_hex_1 (.d(_74126_1_pin3), .dp(1'b0));
endmodule
