// Digital circuit 8bit alu.dig as structural Verilog
module _8bit_alu (
  input  [7:0] in_1,
  input  in_2
);

  wire _7404_1_pin10, _7404_1_pin12, _7404_2_p5, _7404_2_p9, _7404_2_p12, _74283_1_pin2, _74283_1_pin6,
       _74283_1_pin9, _74283_1_pin11, _74283_1_pin15, _74283_2_pin9, _74283_2_pin11, _74283_2_pin15,
       _74574_1_pin12, _74574_1_pin13, _74574_1_pin14, _74574_1_pin15, _74574_1_pin16, _74574_1_pin17,
       _74574_1_pin18, _74574_1_pin19, _74574_2_pin12, _74574_2_pin13, _74574_2_pin14, _74574_2_pin15,
       _74574_2_pin16, _74574_2_pin17, _74574_2_pin18, _74574_2_pin19, CLK, LDA, LDB;
  wire [3:0] _74245_1_pin11, _74245_1_pin15;

  Button button_1 (.out(CLK));
  DipSwitch u_LDA (.out(LDA));
  DipSwitch u_LDB (.out(LDB));
  _74245 _74245_1 (
    .pin1(1'b0), .pin10(1'b0), .pin11(_74245_1_pin11[3]), .pin12(_74245_1_pin11[2]),
    .pin13(_74245_1_pin11[1]), .pin14(_74245_1_pin11[0]), .pin15(_74245_1_pin15[3]),
    .pin16(_74245_1_pin15[2]), .pin17(_74245_1_pin15[1]), .pin18(_74245_1_pin15[0]), .pin19(1'b0),
    .pin20(1'b1));  // open: pin2, pin3, pin4, pin5, pin6, pin7, pin8, pin9
  _74574 _74574_1 (
    .pin1(1'b0), .pin2(in_1[0]), .pin3(in_1[1]), .pin4(in_1[2]), .pin5(in_1[3]), .pin6(in_1[4]),
    .pin7(in_1[5]), .pin8(in_1[6]), .pin9(in_1[7]), .pin10(1'b0), .pin11(LDA), .pin12(_74574_1_pin12),
    .pin13(_74574_1_pin13), .pin14(_74574_1_pin14), .pin15(_74574_1_pin15), .pin16(_74574_1_pin16),
    .pin17(_74574_1_pin17), .pin18(_74574_1_pin18), .pin19(_74574_1_pin19), .pin20(1'b1));
  _74574 _74574_2 (
    .pin1(1'b0), .pin2(in_1[0]), .pin3(in_1[1]), .pin4(in_1[2]), .pin5(in_1[3]), .pin6(in_1[4]),
    .pin7(in_1[5]), .pin8(in_1[6]), .pin9(in_1[7]), .pin10(1'b0), .pin11(LDB), .pin12(_74574_2_pin12),
    .pin13(_74574_2_pin13), .pin14(_74574_2_pin14), .pin15(_74574_2_pin15), .pin16(_74574_2_pin16),
    .pin17(_74574_2_pin17), .pin18(_74574_2_pin18), .pin19(_74574_2_pin19), .pin20(1'b1));
  _74283 _74283_1 (
    .pin1(_74245_1_pin15[1]), .pin2(_74283_1_pin2), .pin3(_74574_1_pin18), .pin4(_74245_1_pin15[0]),
    .pin5(_74574_1_pin19), .pin6(_74283_1_pin6), .pin7(1'b1), .pin8(1'b0), .pin9(_74283_1_pin9),
    .pin10(_74245_1_pin15[3]), .pin11(_74283_1_pin11), .pin12(_74574_1_pin16), .pin13(_74245_1_pin15[2]),
    .pin14(_74574_1_pin17), .pin15(_74283_1_pin15), .pin16(1'b1));
  _7404 _7404_1 (
    .pin1(_74574_2_pin19), .pin2(_74283_1_pin6), .pin3(_74574_2_pin18), .pin4(_74283_1_pin2),
    .pin5(_74574_2_pin17), .pin6(_74283_1_pin15), .pin7(1'b0), .pin8(_74283_1_pin11), .pin9(_74574_2_pin16),
    .pin10(_7404_1_pin10), .pin11(_74574_2_pin15), .pin12(_7404_1_pin12), .pin13(_74574_2_pin14), .pin14(1'b1));
  Seven_Seg_Hex seven_seg_hex_1 (.d(_74245_1_pin15), .dp(1'b0));
  _74283 _74283_2 (
    .pin1(_74245_1_pin11[1]), .pin2(_7404_1_pin12), .pin3(_74574_1_pin14), .pin4(_74245_1_pin11[0]),
    .pin5(_74574_1_pin15), .pin6(_7404_1_pin10), .pin7(_74283_1_pin9), .pin8(1'b0), .pin9(_74283_2_pin9),
    .pin10(_74245_1_pin11[3]), .pin11(_74283_2_pin11), .pin12(_74574_1_pin12), .pin13(_74245_1_pin11[2]),
    .pin14(_74574_1_pin13), .pin15(_74283_2_pin15), .pin16(1'b1));
  // _7404 _7404_2: pin names not known; wires that end beside it: 1'b1, _74574_2_pin13, 1'b0, _74283_2_pin15, _7404_2_p5, _74574_2_pin12, 1'b0, _74283_2_pin11, _7404_2_p9, 1'b0, 1'b0, _7404_2_p12, 1'b0
  LED led_1 (.in(_7404_2_p5));
  LED led_2 (.in(_7404_2_p9));
  LED led_3 (.in(_74283_2_pin9));
  LED led_4 (.in(_7404_2_p12));
  Seven_Seg_Hex seven_seg_hex_2 (.d(_74245_1_pin11), .dp(1'b0));
endmodule
