// Digital circuit alu.dig as structural Verilog
module alu (
  input  [7:0] B,
  input  [7:0] A,
  input  EALU,
  output [7:0] S,
  output LEQ0
);

  wire bitselector_1_out, comparator_1_eq, pulldown_1_out, sub_1_c_o;
  wire [7:0] sub_1_s;

  Sub #(.Bits(8)) sub_1 (.a(B), .b(A), .c_i(pulldown_1_out), .s(sub_1_s), .c_o(sub_1_c_o));
  PullDown pulldown_1 (.out(pulldown_1_out));
  PullDown pulldown_2 (.out(sub_1_c_o));
  Comparator #(.Bits(8)) comparator_1 (.a(sub_1_s), .b({8{1'b0}}), .eq(comparator_1_eq));  // open: gt, lt
  BitSelector #(.Selector_Bits(3)) bitselector_1 (.in(sub_1_s), .sel(3'b111), .out(bitselector_1_out));
  assign S = EALU ? sub_1_s : 8'bz;  // Driver driver_1
  or or_1 (LEQ0, comparator_1_eq, bitselector_1_out);
endmodule
