// Digital circuit main.dig as structural Verilog
module main (
  input  [3:0] in_1,
  input  [3:0] in_2,
  input  in_3,
  input  in_4,
  input  in_5
);

  wire _74283_1_pin9, _74574_1_pin12, _74574_1_pin13, _74574_1_pin14, _74574_1_pin15, _74574_1_pin16,
       _74574_1_pin17, _74574_1_pin18, _74574_1_pin19;
  wire [3:0] _74283_1_pin1;

  _74574 _74574_1 (
    .pin1(in_4), .pin2(in_1[0]), .pin3(in_1[1]), .pin4(in_1[2]), .pin5(in_1[3]), .pin6(in_2[0]),
    .pin7(in_2[1]), .pin8(in_2[2]), .pin9(in_2[3]), .pin10(1'b0), .pin11(in_3), .pin12(_74574_1_pin12),
    .pin13(_74574_1_pin13), .pin14(_74574_1_pin14), .pin15(_74574_1_pin15), .pin16(_74574_1_pin16),
    .pin17(_74574_1_pin17), .pin18(_74574_1_pin18), .pin19(_74574_1_pin19), .pin20(1'b1));
  _74283 _74283_1 (
    .pin1(_74283_1_pin1[1]), .pin2(_74574_1_pin14), .pin3(_74574_1_pin18), .pin4(_74283_1_pin1[0]),
    .pin5(_74574_1_pin19), .pin6(_74574_1_pin15), .pin7(in_5), .pin8(1'b0), .pin9(_74283_1_pin9),
    .pin10(_74283_1_pin1[3]), .pin11(_74574_1_pin12), .pin12(_74574_1_pin16), .pin13(_74283_1_pin1[2]),
    .pin14(_74574_1_pin17), .pin15(_74574_1_pin13), .pin16(1'b1));
  Seven_Seg_Hex seven_seg_hex_1 (.d(_74283_1_pin1), .dp(_74283_1_pin9));
endmodule
