// Digital circuit pause.dig as structural Verilog
module pause (
  input  Pause2,
  input  P,
  input  lt,
  input  Pause1,
  output Y
);

  wire nand_2_out, nand_3_out, nand_4_out, nand_5_out, nand_6_out, nand_7_out;

  nand nand_1 (Y, nand_3_out, nand_2_out);
  nand nand_2 (nand_2_out, nand_5_out, P);
  nand nand_3 (nand_3_out, lt, nand_4_out);
  nand nand_4 (nand_4_out, nand_5_out, nand_5_out);
  nand nand_5 (nand_5_out, nand_7_out, nand_6_out);
  nand nand_6 (nand_6_out, Pause1, Pause1);
  nand nand_7 (nand_7_out, Pause2, Pause2);
endmodule
