// Digital circuit real-chips-workspace.dig as structural Verilog
module real_chips_workspace (
  input  in_1,
  input  [15:0] in_2,
  input  in_3,
  input  in_4,
  input  in_5,
  input  in_6,
  input  in_7,
  input  in_8,
  input  in_9
);

  wire _7404_2_pin5, _7404_2_pin9, _7404_3_pin2, _74173_1_pin3, _74173_1_pin4, _74173_1_pin5, _74173_1_pin6,
       _74173_2_pin4, _74173_2_pin5, _74173_2_pin6, _74181_1_pin1, _74181_1_pin9, _74181_1_pin10,
       _74181_1_pin11, _74245_1_pin5, _74245_1_pin11, _74245_1_pin12, _74245_1_pin13, _74245_1_pin14,
       _74245_1_pin15, _74245_1_pin16, _74245_1_pin17, _74245_1_pin18, _74283_1_pin1, _74283_1_pin4,
       _74283_1_pin9, _74283_1_pin10, _74283_1_pin13, _74283_2_pin1, _74283_2_pin4, _74283_2_pin6,
       _74283_2_pin7, _74283_2_pin9, _74283_2_pin10, _74283_2_pin13, _74283_3_pin1, _74283_3_pin4,
       _74283_3_pin10, _74283_3_pin13, _74283_4_pin1, _74283_4_pin4, _74283_4_pin10, _74283_4_pin13,
       _74283_5_pin9, _74283_6_pin9, _74283_7_pin9, _74283_8_pin9, _74377_1_pin2, _74377_1_pin5,
       _74377_1_pin6, _74377_1_pin9, _74377_2_p3, _74377_3_pin2, _74377_3_pin5, _74377_3_pin6, _74377_3_pin9,
       _74377_3_pin12, _74377_3_pin15, _74377_3_pin16, _74377_3_pin19, _74377_4_pin2, _74377_4_pin5,
       _74377_4_pin6, _74377_4_pin9, _74377_4_pin12, _74377_4_pin15, _74377_4_pin16, _74377_4_pin19,
       _74377_5_pin2, _74377_5_pin5, _74377_5_pin6, _74377_5_pin9, _74377_5_pin12, _74377_5_pin15,
       _74377_5_pin16, _74377_5_pin19, _74377_6_pin2, _74377_6_pin5, _74377_6_pin6, _74377_6_pin12,
       _74377_6_pin15, _74377_6_pin16, CLK, LDA, LDB, notconnected_1_out, notconnected_2_out,
       notconnected_3_out, undriven;
  wire [3:0] _74283_5_pin13, _74283_6_pin1, _74283_7_pin1, _74283_8_pin1, _74574_1_pin15, _74574_1_pin17,
       _74574_2_pin15, _74574_2_pin19, _74574_3_pin15, _74574_3_pin19, _74574_4_pin15, _74574_4_pin19;

  _74377 _74377_1 (
    .pin1(LDA), .pin2(_74377_1_pin2), .pin5(_74377_1_pin5), .pin6(_74377_1_pin6), .pin9(_74377_1_pin9),
    .pin10(1'b0), .pin11(CLK), .pin20(1'b1));  // open: pin3, pin4, pin7, pin8, pin12, pin13, pin14, pin15, pin16, pin17, pin18, pin19
  // _74377 _74377_2: pin names not known; wires that end beside it: 1'b1, LDB, _74377_2_p3
  _74173 _74173_1 (
    .pin1(1'b0), .pin2(1'b0), .pin3(_74173_1_pin3), .pin4(_74173_1_pin4), .pin5(_74173_1_pin5),
    .pin6(_74173_1_pin6), .pin7(CLK), .pin8(1'b0), .pin9(in_4), .pin10(1'b0), .pin11(in_9), .pin12(in_8),
    .pin13(in_7), .pin14(in_6), .pin16(1'b1));  // open: pin15
  _74181 _74181_1 (
    .pin1(_74181_1_pin1), .pin2(_74173_1_pin3), .pin3(1'b0), .pin4(1'b1), .pin5(1'b1), .pin6(1'b0),
    .pin7(1'b1), .pin8(1'b0), .pin9(_74181_1_pin9), .pin10(_74181_1_pin10), .pin11(_74181_1_pin11),
    .pin12(1'b0));  // open: pin13, pin14, pin15, pin16, pin17, pin18, pin19, pin20, pin21, pin22, pin23, pin24
  // _74181 _74181_2: pin names not known; wires that end beside it: CLK, 1'b0, 1'b1, _74377_2_p3, _74377_1_pin5, _74377_1_pin2, _74377_1_pin6, _74377_1_pin9, 1'b0
  // NotConnected on notconnected_1_out
  LED led_1 (.in(undriven));
  _74173 _74173_2 (
    .pin1(1'b0), .pin2(1'b0), .pin3(_74181_1_pin1), .pin4(_74173_2_pin4), .pin5(_74173_2_pin5),
    .pin6(_74173_2_pin6), .pin7(CLK), .pin8(1'b0), .pin9(in_5), .pin10(1'b0), .pin11(in_9), .pin12(in_8),
    .pin13(in_7), .pin14(in_6), .pin16(1'b1));  // open: pin15
  // NotConnected on notconnected_2_out
  // NotConnected on notconnected_3_out
  _74245 _74245_1 (
    .pin1(1'b1), .pin2(_74181_1_pin9), .pin3(_74181_1_pin10), .pin4(_74181_1_pin11), .pin5(_74245_1_pin5),
    .pin6(1'b0), .pin7(1'b0), .pin8(1'b0), .pin9(1'b0), .pin10(1'b0), .pin11(_74245_1_pin11),
    .pin12(_74245_1_pin12), .pin13(_74245_1_pin13), .pin14(_74245_1_pin14), .pin15(_74245_1_pin15),
    .pin16(_74245_1_pin16), .pin17(_74245_1_pin17), .pin18(_74245_1_pin18), .pin19(1'b1), .pin20(1'b1));
  LED led_2 (.in(_74245_1_pin18));
  LED led_3 (.in(_74245_1_pin17));
  LED led_4 (.in(_74245_1_pin16));
  // NotConnected on _74245_1_pin14
  LED led_5 (.in(_74245_1_pin15));
  // NotConnected on _74245_1_pin13
  // NotConnected on _74245_1_pin12
  // NotConnected on _74245_1_pin11
  // _74181 _74181_3: pin names not known; wires that end beside it: 1'b0, 1'b1
  _74377 _74377_3 (
    .pin1(LDA), .pin2(_74377_3_pin2), .pin5(_74377_3_pin5), .pin6(_74377_3_pin6), .pin9(_74377_3_pin9),
    .pin10(1'b0), .pin11(CLK), .pin12(_74377_3_pin12), .pin15(_74377_3_pin15), .pin16(_74377_3_pin16),
    .pin19(_74377_3_pin19), .pin20(1'b1));  // open: pin3, pin4, pin7, pin8, pin13, pin14, pin17, pin18
  _74377 _74377_4 (
    .pin1(LDA), .pin2(_74377_4_pin2), .pin5(_74377_4_pin5), .pin6(_74377_4_pin6), .pin9(_74377_4_pin9),
    .pin10(1'b0), .pin11(CLK), .pin12(_74377_4_pin12), .pin15(_74377_4_pin15), .pin16(_74377_4_pin16),
    .pin19(_74377_4_pin19), .pin20(1'b1));  // open: pin3, pin4, pin7, pin8, pin13, pin14, pin17, pin18
  _74377 _74377_5 (
    .pin1(LDB), .pin2(_74377_5_pin2), .pin5(_74377_5_pin5), .pin6(_74377_5_pin6), .pin9(_74377_5_pin9),
    .pin10(1'b0), .pin11(CLK), .pin12(_74377_5_pin12), .pin15(_74377_5_pin15), .pin16(_74377_5_pin16),
    .pin19(_74377_5_pin19), .pin20(1'b1));  // open: pin3, pin4, pin7, pin8, pin13, pin14, pin17, pin18
  _74283 _74283_1 (
    .pin1(_74283_1_pin1), .pin3(_74377_3_pin5), .pin4(_74283_1_pin4), .pin5(_74377_3_pin2), .pin8(1'b0),
    .pin9(_74283_1_pin9), .pin10(_74283_1_pin10), .pin12(_74377_3_pin15), .pin13(_74283_1_pin13),
    .pin14(_74377_3_pin12), .pin16(1'b1));  // open: pin2, pin6, pin7, pin11, pin15
  _74283 _74283_2 (
    .pin1(_74283_2_pin1), .pin3(_74377_4_pin5), .pin4(_74283_2_pin4), .pin5(_74377_4_pin2),
    .pin6(_74283_2_pin6), .pin7(_74283_2_pin7), .pin8(1'b0), .pin9(_74283_2_pin9), .pin10(_74283_2_pin10),
    .pin12(_74377_4_pin15), .pin13(_74283_2_pin13), .pin14(_74377_4_pin12), .pin16(1'b1));  // open: pin2, pin11, pin15
  _7404 _7404_1 (
    .pin1(_74377_5_pin6), .pin3(_74377_5_pin5), .pin5(_74377_5_pin2), .pin7(1'b0), .pin9(_74377_5_pin16),
    .pin11(_74377_5_pin15), .pin13(_74377_5_pin12), .pin14(1'b1));  // open: pin2, pin4, pin6, pin8, pin10, pin12
  _7404 _7404_2 (
    .pin1(_74377_5_pin9), .pin5(_7404_2_pin5), .pin7(1'b0), .pin9(_7404_2_pin9), .pin13(_74377_5_pin19),
    .pin14(1'b1));  // open: pin2, pin3, pin4, pin6, pin8, pin10, pin11, pin12
  _74283 _74283_3 (
    .pin1(_74283_3_pin1), .pin3(_74377_3_pin9), .pin4(_74283_3_pin4), .pin5(_74377_3_pin6),
    .pin7(_74283_1_pin9), .pin8(1'b0), .pin9(_74283_2_pin7), .pin10(_74283_3_pin10), .pin12(_74377_3_pin19),
    .pin13(_74283_3_pin13), .pin14(_74377_3_pin16), .pin16(1'b1));  // open: pin2, pin6, pin11, pin15
  _74283 _74283_4 (
    .pin1(_74283_4_pin1), .pin3(_74377_4_pin9), .pin4(_74283_4_pin4), .pin5(_74377_4_pin6),
    .pin7(_74283_2_pin9), .pin8(1'b0), .pin10(_74283_4_pin10), .pin12(_74377_4_pin19),
    .pin13(_74283_4_pin13), .pin14(_74377_4_pin16), .pin16(1'b1));  // open: pin2, pin6, pin9, pin11, pin15
  _74377 _74377_6 (
    .pin1(LDB), .pin2(_74377_6_pin2), .pin5(_74377_6_pin5), .pin6(_74377_6_pin6), .pin9(_7404_2_pin5),
    .pin10(1'b0), .pin11(CLK), .pin12(_74377_6_pin12), .pin15(_74377_6_pin15), .pin16(_74377_6_pin16),
    .pin19(_7404_2_pin9), .pin20(1'b1));  // open: pin3, pin4, pin7, pin8, pin13, pin14, pin17, pin18
  _74245 _74245_2 (
    .pin2(_74283_1_pin4), .pin3(_74283_1_pin1), .pin4(_74283_3_pin4), .pin5(_74283_3_pin1),
    .pin6(_74283_1_pin13), .pin7(_74283_1_pin10), .pin8(_74283_3_pin13), .pin9(_74283_3_pin10), .pin10(1'b0),
    .pin20(1'b1));  // open: pin1, pin11, pin12, pin13, pin14, pin15, pin16, pin17, pin18, pin19
  _74245 _74245_3 (
    .pin2(_74283_2_pin4), .pin3(_74283_2_pin1), .pin4(_74283_4_pin4), .pin5(_74283_4_pin1),
    .pin6(_74283_2_pin13), .pin7(_74283_2_pin10), .pin8(_74283_4_pin13), .pin9(_74283_4_pin10), .pin10(1'b0),
    .pin20(1'b1));  // open: pin1, pin11, pin12, pin13, pin14, pin15, pin16, pin17, pin18, pin19
  _7404 _7404_3 (
    .pin1(_74377_6_pin6), .pin2(_7404_3_pin2), .pin3(_74377_6_pin5), .pin5(_74377_6_pin2),
    .pin6(_74283_2_pin6), .pin7(1'b0), .pin9(_74377_6_pin16), .pin11(_74377_6_pin15), .pin13(_74377_6_pin12),
    .pin14(1'b1));  // open: pin4, pin8, pin10, pin12
  Button button_1 (.out(CLK));
  DipSwitch u_LDA (.out(LDA));
  DipSwitch u_LDB (.out(LDB));
  _74574 _74574_1 (
    .pin1(1'b0), .pin2(in_2[0]), .pin3(in_2[1]), .pin4(in_2[2]), .pin5(in_2[3]), .pin6(in_2[4]),
    .pin7(in_2[5]), .pin8(in_2[6]), .pin9(in_2[7]), .pin10(1'b0), .pin11(LDA), .pin12(_74574_1_pin15[3]),
    .pin13(_74574_1_pin15[2]), .pin14(_74574_1_pin15[1]), .pin15(_74574_1_pin15[0]),
    .pin16(_74574_1_pin17[3]), .pin17(_74574_1_pin17[2]), .pin18(_74574_1_pin17[1]),
    .pin19(_74574_1_pin17[0]), .pin20(1'b1));
  _74574 _74574_2 (
    .pin1(1'b0), .pin2(in_2[0]), .pin3(in_2[1]), .pin4(in_2[2]), .pin5(in_2[3]), .pin6(in_2[4]),
    .pin7(in_2[5]), .pin8(in_2[6]), .pin9(in_2[7]), .pin10(1'b0), .pin11(LDB), .pin12(_74574_2_pin15[3]),
    .pin13(_74574_2_pin15[2]), .pin14(_74574_2_pin15[1]), .pin15(_74574_2_pin15[0]),
    .pin16(_74574_2_pin19[3]), .pin17(_74574_2_pin19[2]), .pin18(_74574_2_pin19[1]),
    .pin19(_74574_2_pin19[0]), .pin20(1'b1));
  _74283 _74283_5 (
    .pin1(_74283_5_pin13[1]), .pin2(_74574_2_pin19[1]), .pin3(_74574_1_pin17[1]), .pin4(_74283_5_pin13[0]),
    .pin5(_74574_1_pin17[0]), .pin6(_74574_2_pin19[0]), .pin7(in_1), .pin8(1'b0), .pin9(_74283_5_pin9),
    .pin10(_74283_5_pin13[3]), .pin11(_74574_2_pin19[3]), .pin12(_74574_1_pin17[3]),
    .pin13(_74283_5_pin13[2]), .pin14(_74574_1_pin17[2]), .pin15(_74574_2_pin19[2]), .pin16(1'b1));
  Seven_Seg_Hex seven_seg_hex_1 (.d(_74283_5_pin13), .dp(1'b0));
  _74283 _74283_6 (
    .pin1(_74283_6_pin1[1]), .pin2(_74574_2_pin15[1]), .pin3(_74574_1_pin15[1]), .pin4(_74283_6_pin1[0]),
    .pin5(_74574_1_pin15[0]), .pin6(_74574_2_pin15[0]), .pin7(_74283_5_pin9), .pin8(1'b0),
    .pin9(_74283_6_pin9), .pin10(_74283_6_pin1[3]), .pin11(_74574_2_pin15[3]), .pin12(_74574_1_pin15[3]),
    .pin13(_74283_6_pin1[2]), .pin14(_74574_1_pin15[2]), .pin15(_74574_2_pin15[2]), .pin16(1'b1));
  _74574 _74574_3 (
    .pin1(1'b0), .pin2(in_2[8]), .pin3(in_2[9]), .pin4(in_2[10]), .pin5(in_2[11]), .pin6(in_2[12]),
    .pin7(in_2[13]), .pin8(in_2[14]), .pin9(in_2[15]), .pin10(1'b0), .pin11(LDA), .pin12(_74574_3_pin15[3]),
    .pin13(_74574_3_pin15[2]), .pin14(_74574_3_pin15[1]), .pin15(_74574_3_pin15[0]),
    .pin16(_74574_3_pin19[3]), .pin17(_74574_3_pin19[2]), .pin18(_74574_3_pin19[1]),
    .pin19(_74574_3_pin19[0]), .pin20(1'b1));
  Seven_Seg_Hex seven_seg_hex_2 (.d(_74283_6_pin1), .dp(1'b0));
  _74574 _74574_4 (
    .pin1(1'b0), .pin2(in_2[8]), .pin3(in_2[9]), .pin4(in_2[10]), .pin5(in_2[11]), .pin6(in_2[12]),
    .pin7(in_2[13]), .pin8(in_2[14]), .pin9(in_2[15]), .pin10(1'b0), .pin11(LDB), .pin12(_74574_4_pin15[3]),
    .pin13(_74574_4_pin15[2]), .pin14(_74574_4_pin15[1]), .pin15(_74574_4_pin15[0]),
    .pin16(_74574_4_pin19[3]), .pin17(_74574_4_pin19[2]), .pin18(_74574_4_pin19[1]),
    .pin19(_74574_4_pin19[0]), .pin20(1'b1));
  _74283 _74283_7 (
    .pin1(_74283_7_pin1[1]), .pin2(_74574_4_pin19[1]), .pin3(_74574_3_pin19[1]), .pin4(_74283_7_pin1[0]),
    .pin5(_74574_3_pin19[0]), .pin6(_74574_4_pin19[0]), .pin7(_74283_6_pin9), .pin8(1'b0),
    .pin9(_74283_7_pin9), .pin10(_74283_7_pin1[3]), .pin11(_74574_4_pin19[3]), .pin12(_74574_3_pin19[3]),
    .pin13(_74283_7_pin1[2]), .pin14(_74574_3_pin19[2]), .pin15(_74574_4_pin19[2]), .pin16(1'b1));
  Seven_Seg_Hex seven_seg_hex_3 (.d(_74283_7_pin1), .dp(1'b0));
  _74283 _74283_8 (
    .pin1(_74283_8_pin1[1]), .pin2(_74574_4_pin15[1]), .pin3(_74574_3_pin15[1]), .pin4(_74283_8_pin1[0]),
    .pin5(_74574_3_pin15[0]), .pin6(_74574_4_pin15[0]), .pin7(_74283_7_pin9), .pin8(1'b0),
    .pin9(_74283_8_pin9), .pin10(_74283_8_pin1[3]), .pin11(_74574_4_pin15[3]), .pin12(_74574_3_pin15[3]),
    .pin13(_74283_8_pin1[2]), .pin14(_74574_3_pin15[2]), .pin15(_74574_4_pin15[2]), .pin16(1'b1));
  Seven_Seg_Hex seven_seg_hex_4 (.d(_74283_8_pin1), .dp(1'b0));
  LED led_6 (.in(_74283_8_pin9));

  // Notes on the sheet:
  //   REG.AH
  //   REG.BH
  //   REG.AL
  //   ADR.H
  //   ADR.L
  //   REG.BL
  //   YBUF.H
  //   YBUF.L
endmodule
