// Digital circuit sr_driver.dig as structural Verilog
module sr_driver (
  input  D,
  input  R,
  output SO,
  output RO
);

  wire delay_1_out, delay_2_out, not_1_out, not_2_out;

  Delay delay_1 (.in(D), .out(delay_1_out));
  not not_1 (not_1_out, R);
  not not_2 (not_2_out, D);
  Delay delay_2 (.in(R), .out(delay_2_out));
  and and_1 (SO, delay_1_out, not_1_out);
  or or_1 (RO, not_2_out, delay_2_out);
endmodule
