// Digital circuit subleq.dig as structural Verilog
module subleq (
  input  [7:0] UI,
  input  clk,
  input  in_3
);

  wire and_1_out, and_2_out, and_3_out, bitselector_1_out, button_1_out, CLK_t, comparator_1_eq,
       comparator_2_eq, comparator_3_eq, comparator_4_eq, comparator_5_eq, EALU, EMEM, hex_decode_1_p3,
       hex_decode_2_p1, hex_decode_2_p4, hex_decode_2_p6, hex_decode_3_p3, hex_decode_3_p5, hex_decode_4_p3,
       hex_decode_4_p5, hex_decode_5_p3, hex_decode_5_p5, IPRC, LARG, LBRG, LDRG, LEQ0, LPRC, not_1_out,
       not_2_out, or_1_out, PCK, pulldown_1_out, Reset_Program_Counter_out, RISC, SDRG;
  wire [1:1] button_2_out;
  wire [2:0] counter_1_out;
  wire [3:0] hex_decode_1_p1, hex_decode_1_p4, hex_decode_2_p2, hex_decode_2_p5, hex_decode_3_p1,
       hex_decode_3_p4, hex_decode_4_p1, hex_decode_4_p4, hex_decode_5_p1, hex_decode_5_p4;
  wire [3:3] counter_1_out_2;
  wire [7:0] ABUS, alu_1_s, ARG_2_q, BRG_q, DRG_q, hex_decode_1_p2, PCR_out;

  Counter #(.Bits(4)) counter_1 (
    .en(1'b1), .C(CLK_t), .clr(RISC), .out({counter_1_out_2[3], counter_1_out}));  // open: ovf
  Seven_Seg_Hex seven_seg_hex_1 (.d(hex_decode_1_p1), .dp(hex_decode_1_p3));
  Seven_Seg_Hex seven_seg_hex_2 (.d(hex_decode_1_p4), .dp(hex_decode_2_p1));
  // hex_decode hex_decode_1: pin names not known; wires that end beside it: hex_decode_1_p1, hex_decode_1_p2, hex_decode_1_p3, hex_decode_1_p4
  Register #(.Bits(8)) ARG (.D(alu_1_s), .C(CLK_t), .en(LARG), .Q(hex_decode_1_p2));
  Seven_Seg_Hex seven_seg_hex_3 (.d(hex_decode_2_p2), .dp(hex_decode_2_p4));
  Register #(.Bits(8)) BRG (.D(alu_1_s), .C(CLK_t), .en(LBRG), .Q(BRG_q));
  Seven_Seg_Hex seven_seg_hex_4 (.d({LEQ0, counter_1_out}), .dp(pulldown_1_out));
  Seven_Seg_Hex seven_seg_hex_5 (.d(hex_decode_2_p5), .dp(hex_decode_2_p6));
  // hex_decode hex_decode_2: pin names not known; wires that end beside it: hex_decode_2_p1, hex_decode_2_p2, BRG_q, hex_decode_2_p4, hex_decode_2_p5, hex_decode_2_p6
  PullDown pulldown_1 (.out(pulldown_1_out));
  ROM #(.AddrBits(4), .Bits(9)) ISM (
    .A({LEQ0, counter_1_out}), .sel(1'b1), .D({RISC, LPRC, IPRC, EALU, LBRG, LARG, LDRG, EMEM, SDRG}));
  alu alu_1 (.B(BRG_q), .A(hex_decode_1_p2), .EALU(EALU), .S(alu_1_s), .LEQ0(LEQ0));
  Seven_Seg_Hex seven_seg_hex_6 (.d(hex_decode_3_p1), .dp(hex_decode_3_p3));
  Seven_Seg_Hex seven_seg_hex_7 (.d(hex_decode_3_p4), .dp(hex_decode_3_p5));
  // hex_decode hex_decode_3: pin names not known; wires that end beside it: hex_decode_3_p1, alu_1_s, hex_decode_3_p3, hex_decode_3_p4, hex_decode_3_p5
  PullDown #(.Bits(8)) pulldown_2 (.out(alu_1_s));
  RAMSinglePort #(.AddrBits(8), .isProgramMemory("true"), .Bits(8)) MEM (
    .A(ABUS), .str(EALU), .C(CLK_t), .ld(and_1_out), .D(alu_1_s));
  assign ABUS = not_2_out ? PCR_out : 8'bz;  // Driver driver_1
  CounterPreset #(.Bits(8)) PCR (
    .en(IPRC), .C(CLK_t), .dir(1'b0), .in(alu_1_s), .ld(LPRC), .clr(Reset_Program_Counter_out), .out(PCR_out));  // open: ovf
  not not_1 (not_1_out, bitselector_1_out);
  and and_1 (and_1_out, EMEM, not_1_out);
  not not_2 (not_2_out, SDRG);
  Register #(.Bits(8)) DRG (.D(alu_1_s), .C(CLK_t), .en(LDRG), .Q(DRG_q));
  BitSelector #(.Selector_Bits(3)) bitselector_1 (.in(ABUS), .sel(3'b111), .out(bitselector_1_out));
  assign ABUS = SDRG ? DRG_q : 8'bz;  // Driver driver_2
  assign alu_1_s = and_3_out ? UI : 8'bz;  // Driver driver_3
  Register #(.Bits(8)) ARG_2 (.D(alu_1_s), .C(CLK_t), .en(and_2_out), .Q(ARG_2_q));
  and and_2 (and_2_out, comparator_1_eq, EALU);
  Button Reset_Program_Counter (.out(Reset_Program_Counter_out));
  Seven_Seg_Hex seven_seg_hex_8 (.d(hex_decode_4_p1), .dp(hex_decode_4_p3));
  Seven_Seg_Hex seven_seg_hex_9 (.d(hex_decode_4_p4), .dp(hex_decode_4_p5));
  // hex_decode hex_decode_4: pin names not known; wires that end beside it: hex_decode_4_p1, ARG_2_q, hex_decode_4_p3, hex_decode_4_p4, hex_decode_4_p5
  Comparator #(.Bits(8)) comparator_1 (.a(8'hfd), .b(ABUS), .eq(comparator_1_eq));  // open: gt, lt
  Seven_Seg_Hex seven_seg_hex_10 (.d(hex_decode_5_p1), .dp(hex_decode_5_p3));
  and and_3 (and_3_out, comparator_3_eq, EMEM);
  Seven_Seg_Hex seven_seg_hex_11 (.d(hex_decode_5_p4), .dp(hex_decode_5_p5));
  // hex_decode hex_decode_5: pin names not known; wires that end beside it: hex_decode_5_p1, ABUS, hex_decode_5_p3, hex_decode_5_p4, hex_decode_5_p5
  Comparator #(.Bits(8)) comparator_2 (.a(ABUS), .b({8{1'b1}}), .eq(comparator_2_eq));  // open: gt, lt
  // Probe on comparator_2_eq
  Comparator #(.Bits(8)) comparator_3 (.a(8'hfe), .b(ABUS), .eq(comparator_3_eq));  // open: gt, lt
  Stop stop_1 (.stop(button_1_out));
  Button button_1 (.out(button_1_out));
  BitSelector bitselector_2 (.in({button_2_out[1], clk}), .sel(or_1_out), .out(CLK_t));
  assign PCK = comparator_4_eq ? 1'b1 : 1'bz;  // Driver driver_4
  PullDown pulldown_3 (.out(PCK));
  or or_1 (or_1_out, in_3, PCK);
  Button button_2 (.out(button_2_out[1]));
  Comparator #(.Bits(8)) comparator_4 (.a({8{1'b1}}), .b(ABUS), .eq(comparator_4_eq));  // open: gt, lt
  assign PCK = comparator_5_eq ? 1'b1 : 1'bz;  // Driver driver_5
  Comparator #(.Bits(8)) comparator_5 (.a(8'hfe), .b(ABUS), .eq(comparator_5_eq));  // open: gt, lt

  // Other names for the same wires on the sheet: LDOM = EALU; LMEM = EALU

  // Notes on the sheet:
  //   ISM[0x0] = EMEM + LDRG                # load mem[pc] (&A) into ADDR reg
  //   ISM[0x1] = SADR + EMEM + LARG + IPRC  # load mem[&A] into A reg and pc++
  //   ISM[0x2] = EMEM + LDRG                # load mem[pc] (&B) into ADDR reg
  //   ISM[0x3] = SADR + EMEM + LBRG         # load mem[&B] into B addr reg
  //   ISM[0x4] = SDRG + LDOM + IPRC                # load alu out into mem[&B] and pc++
  //   # if leq0=0
  //   ISM[0x5] = IPRC + RISC                # pc++ and reset inctruction counter
  //   # if leq0=1
  //   ISM[0xd] = EMEM + LPRC + RISC         # load mem[pc] (&C) into pc and reset inctruction counter
  //   ISM[0x8] = ISM[0x0]
  //   ISM[0x9] = ISM[0x1]
  //   ISM[0xa] = ISM[0x2]
  //   ISM[0xb] = ISM[0x3]
  //   ISM[0xc] = ISM[0x4]
  //   contents of ISM (hex, n*v repeats v):
  //   6,4b,6,13,61,140,0,0,6,4b,6,13,61,182
endmodule
