// Digital circuit subleq3.dig as structural Verilog
module subleq3 (
  input  [7:0] UI,
  input  in_2,
  input  clk,
  input  in_4
);

  wire acs, and_1_out, and_2_out, and_3_out, button_1_out, comparator_1_eq, comparator_2_eq, comparator_3_eq,
       comparator_4_eq, comparator_5_eq, inc, jmp, lda, ldb, ldi, ldj, LEQ0, lt, or_1_out, pause, rdb, rst,
       wrt;
  wire [3:0] alu_1_s, alu_1_s_2, ARG_2_q;
  wire [4:0] counter_1_out;
  wire [7:0] ARG_q, BRG_q;
  wire [7:4] ARG_2_q_2;
  wire [15:0] ABUS, ADR0_q, PCR_out;

  or or_1 (or_1_out, rst, in_2);
  Seven_Seg_Hex seven_seg_hex_1 (.d(ARG_q[7:4]), .dp(1'b0));
  Seven_Seg_Hex seven_seg_hex_2 (.d(ARG_q[3:0]), .dp(1'b0));
  Register #(.Bits(8)) ARG (.D({alu_1_s_2, alu_1_s}), .C(lt), .en(lda), .Q(ARG_q));
  Counter #(.Bits(5)) counter_1 (.en(1'b1), .C(lt), .clr(or_1_out), .out(counter_1_out));  // open: ovf
  Seven_Seg_Hex seven_seg_hex_3 (.d(BRG_q[7:4]), .dp(1'b0));
  Seven_Seg_Hex seven_seg_hex_4 (.d(BRG_q[3:0]), .dp(1'b0));
  Register #(.Bits(8)) BRG (.D({alu_1_s_2, alu_1_s}), .C(lt), .en(ldb), .Q(BRG_q));
  ROM #(.AddrBits(5), .Bits(10)) ISM (
    .A({LEQ0, counter_1_out[3:0]}), .sel(1'b1), .D({rst, jmp, inc, wrt, ldb, lda, ldj, ldi, rdb, acs}));
  alu alu_1 (.B(BRG_q), .A(ARG_q), .EALU(wrt), .S({alu_1_s_2, alu_1_s}), .LEQ0(LEQ0));
  Seven_Seg_Hex seven_seg_hex_5 (.d(alu_1_s_2), .dp(1'b0));
  assign pause = comparator_1_eq ? 1'b1 : 1'bz;  // Driver driver_1
  Seven_Seg_Hex seven_seg_hex_6 (.d(alu_1_s), .dp(1'b0));
  PullDown #(.Bits(8)) pulldown_1 (.out({alu_1_s_2, alu_1_s}));
  Comparator #(.Bits(16)) comparator_1 (.a({16{1'b1}}), .b(ABUS), .eq(comparator_1_eq));  // open: gt, lt
  RAMSinglePort #(.AddrBits(12), .isProgramMemory("true"), .Bits(8)) MEM (
    .A(ABUS[11:0]), .str(wrt), .C(lt), .ld(and_1_out), .D({alu_1_s_2, alu_1_s}));
  assign {alu_1_s_2, alu_1_s} = and_2_out ? UI : 8'bz;  // Driver driver_2
  and and_1 (and_1_out, comparator_2_eq, rdb);
  and and_2 (and_2_out, comparator_4_eq, rdb);
  Seven_Seg_Hex seven_seg_hex_7 (.d(ARG_2_q_2), .dp(1'b0));
  Register #(.Bits(8)) ARG_2 (.D({alu_1_s_2, alu_1_s}), .C(lt), .en(and_3_out), .Q({ARG_2_q_2, ARG_2_q}));
  and and_3 (and_3_out, comparator_3_eq, wrt);
  Comparator #(.Bits(4)) comparator_2 (.a(ABUS[15:12]), .b(4'b0000), .eq(comparator_2_eq));  // open: gt, lt
  Register #(.Bits(8)) ADR1 (.D({alu_1_s_2, alu_1_s}), .C(lt), .en(ldj), .Q(ADR0_q[15:8]));
  Register #(.Bits(8)) ADR0 (.D({alu_1_s_2, alu_1_s}), .C(lt), .en(ldi), .Q(ADR0_q[7:0]));
  Seven_Seg_Hex seven_seg_hex_8 (.d(ARG_2_q), .dp(1'b0));
  Comparator #(.Bits(16)) comparator_3 (.a(16'he001), .b(ABUS), .eq(comparator_3_eq));  // open: gt, lt
  assign ABUS = acs ? ADR0_q : 16'bz;  // Driver driver_3
  Comparator #(.Bits(16)) comparator_4 (.a(16'he000), .b(ABUS), .eq(comparator_4_eq));  // open: gt, lt
  CounterPreset #(.Bits(16)) PCR (
    .en(inc), .C(lt), .dir(1'b0), .in(ADR0_q), .ld(jmp), .clr(in_2), .out(PCR_out));  // open: ovf
  PullDown pulldown_2 (.out(pause));
  pause pause_1 (.Pause2(in_4), .P(button_1_out), .lt(clk), .Pause1(pause), .Y(lt));
  assign ABUS = ~acs ? PCR_out : 16'bz;  // DriverInvSel driverinvsel_1
  assign pause = comparator_5_eq ? 1'b1 : 1'bz;  // Driver driver_4
  Button button_1 (.out(button_1_out));
  Comparator #(.Bits(16)) comparator_5 (.a(16'he000), .b(ABUS), .eq(comparator_5_eq));  // open: gt, lt
  Seven_Seg_Hex seven_seg_hex_9 (.d(ABUS[15:12]), .dp(1'b0));
  Seven_Seg_Hex seven_seg_hex_10 (.d(ABUS[11:8]), .dp(1'b0));
  Seven_Seg_Hex seven_seg_hex_11 (.d(ABUS[7:4]), .dp(1'b0));
  Seven_Seg_Hex seven_seg_hex_12 (.d(ABUS[3:0]), .dp(1'b0));

  // Other names for the same wires on the sheet: ABUSH[3:0] = ABUS[15:12]; reset = in_2

  // Notes on the sheet:
  //   in_2: default 1
  //   clk: Hz: 5
  //   ISM[0x0] = EMEM + LDRG                # load mem[pc] (&A) into ADDR reg
  //   ISM[0x1] = SADR + EMEM + LARG + IPRC  # load mem[&A] into A reg and pc++
  //   ISM[0x2] = EMEM + LDRG                # load mem[pc] (&B) into ADDR reg
  //   ISM[0x3] = SADR + EMEM + LBRG         # load mem[&B] into B addr reg
  //   ISM[0x4] = SDRG + LDOM + IPRC                # load alu out into mem[&B] and pc++
  //   # if leq0=0
  //   ISM[0x5] = IPRC + RISC                # pc++ and reset inctruction counter
  //   # if leq0=1
  //   ISM[0xd] = EMEM + LPRC + RISC         # load mem[pc] (&C) into pc and reset inctruction counter
  //   ISM[0x8] = ISM[0x0]
  //   ISM[0x9] = ISM[0x1]
  //   ISM[0xa] = ISM[0x2]
  //   ISM[0xb] = ISM[0x3]
  //   ISM[0xc] = ISM[0x4]
  //   contents of ISM (hex, n*v repeats v):
  //   86,a,93,86,a,23,c1,80,280,7*0,86,a,93,86,a,23,c1,86,a,300
  //   Halt
  //   If the top 4 bits of ABUS=0
  //      AND rdb
  //   then write memory at ABUS to BUS
  //   Program Counter
  //   Count up write to ABUS
  //   unless (acs) is high, then switch ABUS to register input
  //   Pause for user
endmodule
